# Fritzing sketch Conexiones Batisfera (saved by Fritzing 0.9.3b)

parts:
  Componente1 = Arduino Uno (Rev3) - ICSP
  Componente5 = Bluetooth HC-05 Macho
  Componente6 = Speed Sensor
  S1 = Toggle Switch [package=THT]
  BAT1 = BC9VPC [package=bc9vpc]
  BAT2 = BC9VPC [package=bc9vpc]
  L298N1 = L298N motor driver
  M1 = DC Motor

nets:
  N1: Componente1.D8, L298N1.connector15
  N2: Componente1.D9_PWM, L298N1.connector16
  N3: Componente1.D10_PWM/SS, L298N1.connector12
  GND: Componente1.GND, Componente5.GND, Componente6.connector1, S1.L1, L298N1.connector6
  N4: Componente1.D0/RX, Componente5.TXD
  N5: Componente1.D1/TX, Componente5.RXD
  N6: Componente1.D2, Componente6.connector2
  N7: Componente1.3V3, Componente6.connector0
  5V: Componente1.5V, Componente5.VCC
  N8: Componente1.VIN, L298N1.connector7
  N9: S1.L2, BAT2.V-
  N10: BAT1.V+, L298N1.connector5
  N11: BAT1.V-, BAT2.V+
  N12: L298N1.connector2, M1.pin_2
  N13: L298N1.connector4, M1.pin_1
